# Fritzing sketch hippyBallOfLife (saved by Fritzing 0.9.3b)

parts:
  WeMos_D1_Mini1 = WeMos D1 Mini
  GY1 = MPU-6050 Board GY-521 [form="♀ (female)" package=THT]
  NEOPIXEL1 = Neopixel Strip -- Black (30/m)

nets:
  5V: WeMos_D1_Mini1.5V, GY1.pin1, NEOPIXEL1.+5V
  N1: WeMos_D1_Mini1.D1, GY1.pin3
  N2: WeMos_D1_Mini1.D2, GY1.pin4
  N3: WeMos_D1_Mini1.D4, NEOPIXEL1.Din
  N4: WeMos_D1_Mini1.G, GY1.pin2, NEOPIXEL1.GND

custom parts:
  MPU-6050 Board GY-521: Acelerometro y Giroscopio MPU-6050 Board GY-521
  Neopixel Strip -- Black (30/m): These NeoPixel strips have 30 digitally-addressable pixel LEDs per meter and are very affordable and are only 12.5 mm wide, 10 mm if you remove the strip from the casing.
